// Digital circuit 1x15sram.dig as structural Verilog
module _1x15sram (
  input  [14:0] WD__14_0,
  input  WS,
  input  RS1,
  input  RS2,
  input  CLK,
  output [14:0] RD1__14_0,
  output [14:0] RD2__14_0
);

  _1x1sram _1x1sram_1 (
    .WD(WD__14_0[0]), .WS(WS), .RS1(RS1), .RS2(RS2), .CLK(CLK), .RD1(RD1__14_0[0]), .RD2(RD2__14_0[0]));
  _1x1sram _1x1sram_2 (
    .WD(WD__14_0[4]), .WS(WS), .RS1(RS1), .RS2(RS2), .CLK(CLK), .RD1(RD1__14_0[4]), .RD2(RD2__14_0[4]));
  _1x1sram _1x1sram_3 (
    .WD(WD__14_0[8]), .WS(WS), .RS1(RS1), .RS2(RS2), .CLK(CLK), .RD1(RD1__14_0[8]), .RD2(RD2__14_0[8]));
  _1x1sram _1x1sram_4 (
    .WD(WD__14_0[12]), .WS(WS), .RS1(RS1), .RS2(RS2), .CLK(CLK), .RD1(RD1__14_0[12]), .RD2(RD2__14_0[12]));
  _1x1sram _1x1sram_5 (
    .WD(WD__14_0[1]), .WS(WS), .RS1(RS1), .RS2(RS2), .CLK(CLK), .RD1(RD1__14_0[1]), .RD2(RD2__14_0[1]));
  _1x1sram _1x1sram_6 (
    .WD(WD__14_0[5]), .WS(WS), .RS1(RS1), .RS2(RS2), .CLK(CLK), .RD1(RD1__14_0[5]), .RD2(RD2__14_0[5]));
  _1x1sram _1x1sram_7 (
    .WD(WD__14_0[9]), .WS(WS), .RS1(RS1), .RS2(RS2), .CLK(CLK), .RD1(RD1__14_0[9]), .RD2(RD2__14_0[9]));
  _1x1sram _1x1sram_8 (
    .WD(WD__14_0[13]), .WS(WS), .RS1(RS1), .RS2(RS2), .CLK(CLK), .RD1(RD1__14_0[13]), .RD2(RD2__14_0[13]));
  _1x1sram _1x1sram_9 (
    .WD(WD__14_0[2]), .WS(WS), .RS1(RS1), .RS2(RS2), .CLK(CLK), .RD1(RD1__14_0[2]), .RD2(RD2__14_0[2]));
  _1x1sram _1x1sram_10 (
    .WD(WD__14_0[6]), .WS(WS), .RS1(RS1), .RS2(RS2), .CLK(CLK), .RD1(RD1__14_0[6]), .RD2(RD2__14_0[6]));
  _1x1sram _1x1sram_11 (
    .WD(WD__14_0[10]), .WS(WS), .RS1(RS1), .RS2(RS2), .CLK(CLK), .RD1(RD1__14_0[10]), .RD2(RD2__14_0[10]));
  _1x1sram _1x1sram_12 (
    .WD(WD__14_0[14]), .WS(WS), .RS1(RS1), .RS2(RS2), .CLK(CLK), .RD1(RD1__14_0[14]), .RD2(RD2__14_0[14]));
  _1x1sram _1x1sram_13 (
    .WD(WD__14_0[3]), .WS(WS), .RS1(RS1), .RS2(RS2), .CLK(CLK), .RD1(RD1__14_0[3]), .RD2(RD2__14_0[3]));
  _1x1sram _1x1sram_14 (
    .WD(WD__14_0[7]), .WS(WS), .RS1(RS1), .RS2(RS2), .CLK(CLK), .RD1(RD1__14_0[7]), .RD2(RD2__14_0[7]));
  _1x1sram _1x1sram_15 (
    .WD(WD__14_0[11]), .WS(WS), .RS1(RS1), .RS2(RS2), .CLK(CLK), .RD1(RD1__14_0[11]), .RD2(RD2__14_0[11]));

  // Other names for the same wires on the sheet: RD1_0 = RD1__14_0[0]; RD1_1 = RD1__14_0[1]; RD1_2 = RD1__14_0[2];
  //   RD1_3 = RD1__14_0[3]; RD1_4 = RD1__14_0[4]; RD1_5 = RD1__14_0[5]; RD1_6 = RD1__14_0[6]; RD1_7 = RD1__14_0[7];
  //   RD1_8 = RD1__14_0[8]; RD1_9 = RD1__14_0[9]; RD1_10 = RD1__14_0[10]; RD1_11 = RD1__14_0[11];
  //   RD1_12 = RD1__14_0[12]; RD1_13 = RD1__14_0[13]; RD1_14 = RD1__14_0[14]; RD2_0 = RD2__14_0[0];
  //   RD2_1 = RD2__14_0[1]; RD2_2 = RD2__14_0[2]; RD2_3 = RD2__14_0[3]; RD2_4 = RD2__14_0[4]; RD2_5 = RD2__14_0[5];
  //   RD2_6 = RD2__14_0[6]; RD2_7 = RD2__14_0[7]; RD2_8 = RD2__14_0[8]; RD2_9 = RD2__14_0[9]; RD2_10 = RD2__14_0[10];
  //   RD2_11 = RD2__14_0[11]; RD2_12 = RD2__14_0[12]; RD2_13 = RD2__14_0[13]; RD2_14 = RD2__14_0[14];
  //   WD_0 = WD__14_0[0]; WD_1 = WD__14_0[1]; WD_2 = WD__14_0[2]; WD_3 = WD__14_0[3]; WD_4 = WD__14_0[4];
  //   WD_5 = WD__14_0[5]; WD_6 = WD__14_0[6]; WD_7 = WD__14_0[7]; WD_8 = WD__14_0[8]; WD_9 = WD__14_0[9];
  //   WD_10 = WD__14_0[10]; WD_11 = WD__14_0[11]; WD_12 = WD__14_0[12]; WD_13 = WD__14_0[13]; WD_14 = WD__14_0[14]
endmodule
