// Digital circuit 4bit_pc.dig as structural Verilog
module _4bit_pc (
  input  [3:0] I__3_0,
  input  CLK,
  output [3:0] O__3_0
);

  _1bit_reg _1bit_reg_1 (.D_in(I__3_0[0]), .Sel(1'b1), .CLK(CLK), .D_out(O__3_0[0]));
  _1bit_reg _1bit_reg_2 (.D_in(I__3_0[1]), .Sel(1'b1), .CLK(CLK), .D_out(O__3_0[1]));
  _1bit_reg _1bit_reg_3 (.D_in(I__3_0[2]), .Sel(1'b1), .CLK(CLK), .D_out(O__3_0[2]));
  _1bit_reg _1bit_reg_4 (.D_in(I__3_0[3]), .Sel(1'b1), .CLK(CLK), .D_out(O__3_0[3]));
endmodule
