// Digital circuit 6bit_alu.dig as structural Verilog
module _6bit_alu (
  input  [5:0] A__5_0,
  input  [5:0] B__5_0,
  input  [1:0] OP__1_0,
  input  CF_0,
  output [5:0] R__5_0,
  output SF,
  output ZF,
  output CF
);

  wire [2:0] F_0, F_1, F_2;
  wire [5:0] _6bit_full_adder_1_o__5_0, _6bit_shr_1_o__5_0, _6bit_xor_1_o__5_0;

  _6bit_xor _6bit_xor_1 (
    .A__5_0(A__5_0), .B__5_0(B__5_0), .O__5_0(_6bit_xor_1_o__5_0), .SF(F_0[0]), .ZF(F_0[1]), .CF(F_0[2]));
  _6bit_full_adder _6bit_full_adder_1 (
    .A__5_0(A__5_0), .B__5_0(B__5_0), .O__5_0(_6bit_full_adder_1_o__5_0), .CF(F_1[2]), .SF(F_1[0]),
    .ZF(F_1[1]));
  _6bit_shr _6bit_shr_1 (
    .CF_0(CF_0), .A__5_0(A__5_0), .B__5_0(B__5_0), .O__5_0(_6bit_shr_1_o__5_0), .ZF(F_2[1]), .CF(F_2[2]),
    .SF(F_2[0]));
  Multiplexer #(.Selector_Bits(2), .Bits(3)) multiplexer_1 (
    .sel(OP__1_0), .in_0(F_0), .in_1(F_1), .in_2(F_2), .in_3(3'b000), .out({CF, ZF, SF}));
  Multiplexer #(.Bits(6), .Selector_Bits(2)) multiplexer_2 (
    .sel(OP__1_0), .in_0(_6bit_xor_1_o__5_0), .in_1(_6bit_full_adder_1_o__5_0), .in_2(_6bit_shr_1_o__5_0),
    .in_3({6{1'b0}}), .out(R__5_0));

  // Other names for the same wires on the sheet: A[5:0] = A__5_0; B[5:0] = B__5_0
endmodule
