// Digital circuit 6bit_cpu.dig as structural Verilog
module _6bit_cpu (
  input  [3:0] RA2__3_0,
  input  [3:0] WA__3_0,
  input  [14:0] WD__14_0,
  input  WE,
  input  CLK,
  input  PC_EN,
  output [5:0] out_7
);

  wire _6bit_alu_1_cf, _6bit_alu_1_sf, _6bit_alu_1_zf, control_unit_1_im_sel, control_unit_1_jmp_sel,
       control_unit_1_reg_en, CPU_CLK, flag_register_1_cf_out, flag_register_1_sf_out, flag_register_1_zf_out;
  wire [1:0] control_unit_1_op__1_0;
  wire [2:0] dc_2;
  wire [3:0] _4bit_pc_1_o__3_0, _4bit_pca_1_o__3_0, _9x15sram_1_rd1, multiplexer_1_out;
  wire [4:0] dc_0;
  wire [5:0] _6bit_reg_set_1_a__5_0, _6bit_reg_set_1_b__5_0, multiplexer_2_out;
  wire [5:5] im_data;
  wire [6:5] dc_3;

  Multiplexer #(.Bits(4)) multiplexer_1 (
    .sel(control_unit_1_jmp_sel), .in_0(_4bit_pca_1_o__3_0), .in_1({dc_2, im_data[5]}),
    .out(multiplexer_1_out));
  _4bit_pca _4bit_pca_1 (.I__3_0(_4bit_pc_1_o__3_0), .O__3_0(_4bit_pca_1_o__3_0));
  _4bit_pc _4bit_pc_1 (.I__3_0(multiplexer_1_out), .CLK(CPU_CLK), .O__3_0(_4bit_pc_1_o__3_0));
  and and_1 (CPU_CLK, PC_EN, CLK);
  _9x15sram _9x15sram_1 (
    .RA1__3_0(_4bit_pc_1_o__3_0), .RA2__3_0(RA2__3_0), .WA__3_0(WA__3_0), .WD__14_0(WD__14_0), .WE(WE),
    .CLK(CLK), .RD1({_9x15sram_1_rd1, dc_2, im_data[5], dc_3, dc_0}));  // open: RD2
  control_unit control_unit_1 (
    .opcode__3_0(_9x15sram_1_rd1), .jmp_sel(control_unit_1_jmp_sel), .op__1_0(control_unit_1_op__1_0),
    .im_sel(control_unit_1_im_sel), .REG_EN(control_unit_1_reg_en), .ZF(flag_register_1_zf_out),
    .SF(flag_register_1_sf_out), .CF(flag_register_1_cf_out));
  _6bit_reg_set _6bit_reg_set_1 (
    .REG_EN(control_unit_1_reg_en), .WRD__5_0(out_7), .WR__2_0(dc_2), .CLK(CPU_CLK), .RA__2_0(dc_2),
    .RB__2_0({im_data[5], dc_3}), .A__5_0(_6bit_reg_set_1_a__5_0), .B__5_0(_6bit_reg_set_1_b__5_0));
  _6bit_alu _6bit_alu_1 (
    .A__5_0(_6bit_reg_set_1_a__5_0), .B__5_0(multiplexer_2_out), .CF_0(flag_register_1_cf_out),
    .OP__1_0(control_unit_1_op__1_0), .R__5_0(out_7), .SF(_6bit_alu_1_sf), .ZF(_6bit_alu_1_zf),
    .CF(_6bit_alu_1_cf));
  flag_register flag_register_1 (
    .SF(_6bit_alu_1_sf), .ZF(_6bit_alu_1_zf), .CF(_6bit_alu_1_cf), .CLK(CPU_CLK),
    .SF_out(flag_register_1_sf_out), .ZF_out(flag_register_1_zf_out), .CF_out(flag_register_1_cf_out));
  Multiplexer #(.Bits(6)) multiplexer_2 (
    .sel(control_unit_1_im_sel), .in_0(_6bit_reg_set_1_b__5_0), .in_1({im_data[5], dc_3, dc_0[4:2]}),
    .out(multiplexer_2_out));

  // Other names for the same wires on the sheet: dc_1[1:0] = dc_0[1:0]; dc_3[4:0] = dc_0;
  //   im_data[4:0] = {dc_3, dc_0[4:2]}; reg2[2:0] = {im_data[5], dc_3}; jmp_addr[3:0] = {dc_2, im_data[5]};
  //   reg1[2:0] = dc_2
endmodule
