// Digital circuit 6bit_full_adder.dig as structural Verilog
module _6bit_full_adder (
  input  [5:0] B__5_0,
  input  [5:0] A__5_0,
  output [5:0] O__5_0,
  output ZF,
  output CF,
  output SF
);

  wire full_adder_2_c_out, full_adder_3_c_out, full_adder_4_c_out, full_adder_5_c_out, full_adder_6_c_out;

  full_adder full_adder_1 (.C_in(full_adder_2_c_out), .C_out(CF), .S(O__5_0[5]), .A(B__5_0[5]), .B(A__5_0[5]));
  full_adder full_adder_2 (
    .C_in(full_adder_3_c_out), .C_out(full_adder_2_c_out), .S(O__5_0[4]), .A(B__5_0[4]), .B(A__5_0[4]));
  full_adder full_adder_3 (
    .C_in(full_adder_4_c_out), .C_out(full_adder_3_c_out), .S(O__5_0[3]), .A(B__5_0[3]), .B(A__5_0[3]));
  full_adder full_adder_4 (
    .C_in(full_adder_5_c_out), .C_out(full_adder_4_c_out), .S(O__5_0[2]), .A(B__5_0[2]), .B(A__5_0[2]));
  full_adder full_adder_5 (
    .C_in(full_adder_6_c_out), .C_out(full_adder_5_c_out), .S(O__5_0[1]), .A(B__5_0[1]), .B(A__5_0[1]));
  full_adder full_adder_6 (.C_in(1'b0), .C_out(full_adder_6_c_out), .S(O__5_0[0]), .A(B__5_0[0]), .B(A__5_0[0]));
  and and_1 (ZF, ~O__5_0[0], ~O__5_0[1], ~O__5_0[2], ~O__5_0[3], ~O__5_0[4], ~O__5_0[5]);  // And

  assign SF = O__5_0[5];
endmodule
