// Digital circuit 6bit_reg.dig as structural Verilog
module _6bit_reg (
  input  [5:0] D_in__5_0,
  input  SEL,
  input  CLK,
  output [5:0] D_out__5_0
);

  _1bit_reg _1bit_reg_1 (.D_in(D_in__5_0[0]), .Sel(SEL), .CLK(CLK), .D_out(D_out__5_0[0]));
  _1bit_reg _1bit_reg_2 (.D_in(D_in__5_0[1]), .Sel(SEL), .CLK(CLK), .D_out(D_out__5_0[1]));
  _1bit_reg _1bit_reg_3 (.D_in(D_in__5_0[2]), .Sel(SEL), .CLK(CLK), .D_out(D_out__5_0[2]));
  _1bit_reg _1bit_reg_4 (.D_in(D_in__5_0[3]), .Sel(SEL), .CLK(CLK), .D_out(D_out__5_0[3]));
  _1bit_reg _1bit_reg_5 (.D_in(D_in__5_0[4]), .Sel(SEL), .CLK(CLK), .D_out(D_out__5_0[4]));
  _1bit_reg _1bit_reg_6 (.D_in(D_in__5_0[5]), .Sel(SEL), .CLK(CLK), .D_out(D_out__5_0[5]));
endmodule
