// Digital circuit 6bit_reg_set.dig as structural Verilog
module _6bit_reg_set (
  input  [5:0] WRD__5_0,
  input  [2:0] WR__2_0,
  input  REG_EN,
  input  CLK,
  input  [2:0] RA__2_0,
  input  [2:0] RB__2_0,
  output [5:0] A__5_0,
  output [5:0] B__5_0
);

  wire R_0, R_1, R_2, R_3, R_4, SEL_0, SEL_1, SEL_2, SEL_3, SEL_4;
  wire [5:0] _6bit_reg_1_d_out__5_0, _6bit_reg_2_d_out__5_0, _6bit_reg_3_d_out__5_0, _6bit_reg_4_d_out__5_0,
       _6bit_reg_5_d_out__5_0;

  and and_1 (SEL_0, R_0, REG_EN);
  and and_2 (SEL_2, R_2, REG_EN);
  Decoder #(.Selector_Bits(3)) decoder_1 (
    .sel(WR__2_0), .out_0(R_0), .out_1(R_1), .out_2(R_2), .out_3(R_3), .out_4(R_4));  // open: out_5, out_6, out_7
  and and_3 (SEL_4, R_4, REG_EN);
  and and_4 (SEL_1, R_1, REG_EN);
  and and_5 (SEL_3, R_3, REG_EN);
  _6bit_reg _6bit_reg_1 (.D_in__5_0(WRD__5_0), .SEL(SEL_0), .CLK(CLK), .D_out__5_0(_6bit_reg_1_d_out__5_0));
  _6bit_reg _6bit_reg_2 (.D_in__5_0(WRD__5_0), .SEL(SEL_1), .CLK(CLK), .D_out__5_0(_6bit_reg_2_d_out__5_0));
  _6bit_reg _6bit_reg_3 (.D_in__5_0(WRD__5_0), .SEL(SEL_2), .CLK(CLK), .D_out__5_0(_6bit_reg_3_d_out__5_0));
  _6bit_reg _6bit_reg_4 (.D_in__5_0(WRD__5_0), .SEL(SEL_3), .CLK(CLK), .D_out__5_0(_6bit_reg_4_d_out__5_0));
  _6bit_reg _6bit_reg_5 (.D_in__5_0(WRD__5_0), .SEL(SEL_4), .CLK(CLK), .D_out__5_0(_6bit_reg_5_d_out__5_0));
  Multiplexer #(.Bits(6), .Selector_Bits(3)) multiplexer_1 (
    .sel(RA__2_0), .in_0(_6bit_reg_1_d_out__5_0), .in_1(_6bit_reg_2_d_out__5_0),
    .in_2(_6bit_reg_3_d_out__5_0), .in_3(_6bit_reg_4_d_out__5_0), .in_4(_6bit_reg_5_d_out__5_0),
    .in_5({6{1'b0}}), .in_6({6{1'b0}}), .in_7({6{1'b0}}), .out(A__5_0));
  Multiplexer #(.Selector_Bits(3), .Bits(6)) multiplexer_2 (
    .sel(RB__2_0), .in_0(_6bit_reg_1_d_out__5_0), .in_1(_6bit_reg_2_d_out__5_0),
    .in_2(_6bit_reg_3_d_out__5_0), .in_3(_6bit_reg_4_d_out__5_0), .in_4(_6bit_reg_5_d_out__5_0),
    .in_5({6{1'b0}}), .in_6({6{1'b0}}), .in_7({6{1'b0}}), .out(B__5_0));

  // Other names for the same wires on the sheet: A[5:0] = A__5_0; B[5:0] = B__5_0; RA[2:0] = RA__2_0;
  //   RB[2:0] = RB__2_0; WRD[5:0] = WRD__5_0
endmodule
