// Digital circuit 6bit_shr.dig as structural Verilog
module _6bit_shr (
  input  [5:0] A__5_0,
  input  [5:0] B__5_0,
  input  CF_0,
  output [5:0] O__5_0,
  output ZF,
  output SF,
  output CF
);

  wire comparator_1_gt, comparator_2_gt, multiplexer_4_out;
  wire [5:0] O;

  Comparator #(.Bits(6)) comparator_1 (.a(B__5_0), .b(6'b000101), .gt(comparator_1_gt));  // open: eq, lt
  Comparator #(.Bits(6)) comparator_2 (.a(B__5_0), .b(6'b000110), .gt(comparator_2_gt));  // open: eq, lt
  Multiplexer multiplexer_1 (.sel(comparator_2_gt), .in_0(multiplexer_4_out), .in_1(1'b0), .out(CF));
  Multiplexer #(.Bits(6)) multiplexer_2 (.sel(comparator_1_gt), .in_0(O), .in_1({6{1'b0}}), .out(O__5_0));
  Multiplexer #(.Selector_Bits(3)) multiplexer_3 (
    .sel(B__5_0[2:0]), .in_0(A__5_0[5]), .in_1(1'b0), .in_2(1'b0), .in_3(1'b0), .in_4(1'b0), .in_5(1'b0),
    .in_6(1'b0), .in_7(1'b0), .out(O[5]));
  Multiplexer #(.Selector_Bits(3)) multiplexer_4 (
    .sel(B__5_0[2:0]), .in_0(CF_0), .in_1(A__5_0[0]), .in_2(A__5_0[1]), .in_3(A__5_0[2]), .in_4(A__5_0[3]),
    .in_5(A__5_0[4]), .in_6(A__5_0[5]), .in_7(1'b0), .out(multiplexer_4_out));
  Multiplexer #(.Selector_Bits(3)) multiplexer_5 (
    .sel(B__5_0[2:0]), .in_0(A__5_0[4]), .in_1(A__5_0[5]), .in_2(1'b0), .in_3(1'b0), .in_4(1'b0),
    .in_5(1'b0), .in_6(1'b0), .in_7(1'b0), .out(O[4]));
  Multiplexer #(.Selector_Bits(3)) multiplexer_6 (
    .sel(B__5_0[2:0]), .in_0(A__5_0[3]), .in_1(A__5_0[4]), .in_2(A__5_0[5]), .in_3(1'b0), .in_4(1'b0),
    .in_5(1'b0), .in_6(1'b0), .in_7(1'b0), .out(O[3]));
  and and_1 (ZF, ~O__5_0[0], ~O__5_0[1], ~O__5_0[2], ~O__5_0[3], ~O__5_0[4], ~O__5_0[5]);  // And
  Multiplexer #(.Selector_Bits(3)) multiplexer_7 (
    .sel(B__5_0[2:0]), .in_0(A__5_0[2]), .in_1(A__5_0[3]), .in_2(A__5_0[4]), .in_3(A__5_0[5]), .in_4(1'b0),
    .in_5(1'b0), .in_6(1'b0), .in_7(1'b0), .out(O[2]));
  Multiplexer #(.Selector_Bits(3)) multiplexer_8 (
    .sel(B__5_0[2:0]), .in_0(A__5_0[1]), .in_1(A__5_0[2]), .in_2(A__5_0[3]), .in_3(A__5_0[4]),
    .in_4(A__5_0[5]), .in_5(1'b0), .in_6(1'b0), .in_7(1'b0), .out(O[1]));
  Multiplexer #(.Selector_Bits(3)) multiplexer_9 (
    .sel(B__5_0[2:0]), .in_0(A__5_0[0]), .in_1(A__5_0[1]), .in_2(A__5_0[2]), .in_3(A__5_0[3]),
    .in_4(A__5_0[4]), .in_5(A__5_0[5]), .in_6(1'b0), .in_7(1'b0), .out(O[0]));

  assign SF = O__5_0[5];

  // Other names for the same wires on the sheet: A_0 = A__5_0[0]; A_1 = A__5_0[1]; A_2 = A__5_0[2]; A_3 = A__5_0[3];
  //   A_4 = A__5_0[4]; A_5 = A__5_0[5]; B__5_3[2:0] = B__5_0[2:0]; O_final[5:0] = O__5_0
endmodule
