// Digital circuit 6bit_xor.dig as structural Verilog
module _6bit_xor (
  input  [5:0] A__5_0,
  input  [5:0] B__5_0,
  output [5:0] O__5_0,
  output ZF,
  output SF,
  output CF
);

  xor xor_1 (O__5_0[0], A__5_0[0], B__5_0[0]);
  xor xor_2 (O__5_0[1], A__5_0[1], B__5_0[1]);
  xor xor_3 (O__5_0[2], A__5_0[2], B__5_0[2]);
  xor xor_4 (O__5_0[3], A__5_0[3], B__5_0[3]);
  xor xor_5 (O__5_0[4], A__5_0[4], B__5_0[4]);
  xor xor_6 (O__5_0[5], A__5_0[5], B__5_0[5]);
  and and_1 (ZF, ~O__5_0[0], ~O__5_0[1], ~O__5_0[2], ~O__5_0[3], ~O__5_0[4], ~O__5_0[4]);  // And

  assign CF = 1'b0;
  assign SF = O__5_0[5];
endmodule
