// Digital circuit 9x15sram.dig as structural Verilog
module _9x15sram (
  input  [14:0] WD__14_0,
  input  WE,
  input  [3:0] WA__3_0,
  input  [3:0] RA1__3_0,
  input  [3:0] RA2__3_0,
  input  CLK,
  output [14:0] RD1,
  output [14:0] RD2
);

  wire R0, R1, R2, R3, R4, R5, R6, R7, R8, RS1_0, RS1_1, RS1_2, RS1_3, RS1_4, RS1_5, RS1_6, RS1_7, RS1_8,
       RS2_0, RS2_1, RS2_2, RS2_3, RS2_4, RS2_5, RS2_6, RS2_7, RS2_8, WS0, WS1, WS2, WS3, WS4, WS5, WS6, WS7,
       WS8;
  wire [14:0] _1x15sram_1_rd1__14_0, _1x15sram_1_rd2__14_0, _1x15sram_2_rd1__14_0, _1x15sram_2_rd2__14_0,
       _1x15sram_3_rd1__14_0, _1x15sram_3_rd2__14_0, _1x15sram_4_rd1__14_0, _1x15sram_4_rd2__14_0,
       _1x15sram_5_rd1__14_0, _1x15sram_5_rd2__14_0, _1x15sram_6_rd1__14_0, _1x15sram_6_rd2__14_0,
       _1x15sram_7_rd1__14_0, _1x15sram_7_rd2__14_0, _1x15sram_8_rd1__14_0, _1x15sram_8_rd2__14_0,
       _1x15sram_9_rd1__14_0, _1x15sram_9_rd2__14_0;

  Decoder #(.Selector_Bits(4)) decoder_1 (
    .sel(WA__3_0), .out_0(R0), .out_1(R1), .out_2(R2), .out_3(R3), .out_4(R4), .out_5(R5), .out_6(R6),
    .out_7(R7), .out_8(R8));  // open: out_9, out_10, out_11, out_12, out_13, out_14, out_15
  and and_1 (WS0, R0, WE);
  and and_2 (WS2, R2, WE);
  and and_3 (WS4, R4, WE);
  and and_4 (WS6, R6, WE);
  and and_5 (WS8, R8, WE);
  Decoder #(.Selector_Bits(4)) decoder_2 (
    .sel(RA1__3_0), .out_0(RS1_0), .out_1(RS1_1), .out_2(RS1_2), .out_3(RS1_3), .out_4(RS1_4), .out_5(RS1_5),
    .out_6(RS1_6), .out_7(RS1_7), .out_8(RS1_8));  // open: out_9, out_10, out_11, out_12, out_13, out_14, out_15
  and and_6 (WS1, R1, WE);
  and and_7 (WS3, R3, WE);
  and and_8 (WS5, R5, WE);
  and and_9 (WS7, R7, WE);
  Decoder #(.Selector_Bits(4)) decoder_3 (
    .sel(RA2__3_0), .out_0(RS2_0), .out_1(RS2_1), .out_2(RS2_2), .out_3(RS2_3), .out_4(RS2_4), .out_5(RS2_5),
    .out_6(RS2_6), .out_7(RS2_7), .out_8(RS2_8));  // open: out_9, out_10, out_11, out_12, out_13, out_14, out_15
  _1x15sram _1x15sram_1 (
    .WD__14_0(WD__14_0), .WS(WS0), .RS1(RS1_0), .RS2(RS2_0), .CLK(CLK), .RD1__14_0(_1x15sram_1_rd1__14_0),
    .RD2__14_0(_1x15sram_1_rd2__14_0));
  _1x15sram _1x15sram_2 (
    .WD__14_0(WD__14_0), .WS(WS1), .RS1(RS1_1), .RS2(RS2_1), .CLK(CLK), .RD1__14_0(_1x15sram_2_rd1__14_0),
    .RD2__14_0(_1x15sram_2_rd2__14_0));
  _1x15sram _1x15sram_3 (
    .WD__14_0(WD__14_0), .WS(WS2), .RS1(RS1_2), .RS2(RS2_2), .CLK(CLK), .RD1__14_0(_1x15sram_3_rd1__14_0),
    .RD2__14_0(_1x15sram_3_rd2__14_0));
  _1x15sram _1x15sram_4 (
    .WD__14_0(WD__14_0), .WS(WS3), .RS1(RS1_3), .RS2(RS2_3), .CLK(CLK), .RD1__14_0(_1x15sram_4_rd1__14_0),
    .RD2__14_0(_1x15sram_4_rd2__14_0));
  _1x15sram _1x15sram_5 (
    .WD__14_0(WD__14_0), .WS(WS4), .RS1(RS1_4), .RS2(RS2_4), .CLK(CLK), .RD1__14_0(_1x15sram_5_rd1__14_0),
    .RD2__14_0(_1x15sram_5_rd2__14_0));
  _1x15sram _1x15sram_6 (
    .WD__14_0(WD__14_0), .WS(WS5), .RS1(RS1_5), .RS2(RS2_5), .CLK(CLK), .RD1__14_0(_1x15sram_6_rd1__14_0),
    .RD2__14_0(_1x15sram_6_rd2__14_0));
  _1x15sram _1x15sram_7 (
    .WD__14_0(WD__14_0), .WS(WS6), .RS1(RS1_6), .RS2(RS2_6), .CLK(CLK), .RD1__14_0(_1x15sram_7_rd1__14_0),
    .RD2__14_0(_1x15sram_7_rd2__14_0));
  _1x15sram _1x15sram_8 (
    .WD__14_0(WD__14_0), .WS(WS7), .RS1(RS1_7), .RS2(RS2_7), .CLK(CLK), .RD1__14_0(_1x15sram_8_rd1__14_0),
    .RD2__14_0(_1x15sram_8_rd2__14_0));
  _1x15sram _1x15sram_9 (
    .WD__14_0(WD__14_0), .WS(WS8), .RS1(RS1_8), .RS2(RS2_8), .CLK(CLK), .RD1__14_0(_1x15sram_9_rd1__14_0),
    .RD2__14_0(_1x15sram_9_rd2__14_0));
  assign RD1 = _1x15sram_1_rd1__14_0 | _1x15sram_2_rd1__14_0 | _1x15sram_3_rd1__14_0 | _1x15sram_4_rd1__14_0 | _1x15sram_5_rd1__14_0 | _1x15sram_6_rd1__14_0 | _1x15sram_7_rd1__14_0 | _1x15sram_8_rd1__14_0 | _1x15sram_9_rd1__14_0;  // Or or_1, 15 bits wide
  assign RD2 = _1x15sram_1_rd2__14_0 | _1x15sram_2_rd2__14_0 | _1x15sram_3_rd2__14_0 | _1x15sram_4_rd2__14_0 | _1x15sram_5_rd2__14_0 | _1x15sram_6_rd2__14_0 | _1x15sram_7_rd2__14_0 | _1x15sram_8_rd2__14_0 | _1x15sram_9_rd2__14_0;  // Or or_2, 15 bits wide

  // Other names for the same wires on the sheet: RA1[3:0] = RA1__3_0; RA2[3:0] = RA2__3_0; WD[14:0] = WD__14_0
endmodule
