// Digital circuit FA.dig as structural Verilog
module FA (
  input  X,
  input  Y,
  input  Cin,
  output S,
  output cout
);

  wire and_1_out, and_2_out, Cout_t, undriven, xor_1_out;

  xor xor_1 (xor_1_out, X, Y);
  and and_1 (and_1_out, X, Y);
  xor xor_2 (S, xor_1_out, undriven);
  and and_2 (and_2_out, xor_1_out, undriven);
  or or_1 (Cout_t, and_2_out, and_1_out);
endmodule
