// Digital circuit control_unit.dig as structural Verilog
module control_unit (
  input  [3:0] opcode__3_0,
  input  ZF,
  input  SF,
  input  CF,
  output jmp_sel,
  output im_sel,
  output [1:0] op__1_0,
  output REG_EN
);

  wire and_1_out, and_2_out, and_3_out, and_5_out, not_1_out, not_2_out, not_3_out, not_4_out, or_1_out;

  not not_1 (not_1_out, opcode__3_0[0]);
  not not_2 (not_2_out, opcode__3_0[1]);
  not not_3 (not_3_out, opcode__3_0[2]);
  not not_4 (not_4_out, opcode__3_0[3]);
  and and_1 (and_1_out, ~CF, opcode__3_0[0], not_2_out);  // And
  and and_2 (and_2_out, not_1_out, not_2_out);
  and and_3 (and_3_out, not_3_out, opcode__3_0[3]);
  and and_4 (im_sel, not_4_out, opcode__3_0[2]);
  and and_5 (and_5_out, not_4_out, not_3_out);
  or or_1 (or_1_out, and_1_out, and_2_out);
  or or_2 (REG_EN, im_sel, and_5_out);
  and and_6 (jmp_sel, or_1_out, and_3_out);

  assign op__1_0 = opcode__3_0[1:0];
endmodule
