// Digital circuit flag_register.dig as structural Verilog
module flag_register (
  input  SF,
  input  ZF,
  input  CLK,
  input  CF,
  output CF_out,
  output SF_out,
  output ZF_out
);

  _1bit_reg _1bit_reg_1 (.D_in(CF), .Sel(1'b1), .CLK(CLK), .D_out(CF_out));
  _1bit_reg _1bit_reg_2 (.D_in(SF), .Sel(1'b1), .CLK(CLK), .D_out(SF_out));
  _1bit_reg _1bit_reg_3 (.D_in(ZF), .Sel(1'b1), .CLK(CLK), .D_out(ZF_out));

  // Other names for the same wires on the sheet: r0 = CF_out; r1 = SF_out; r2 = ZF_out
endmodule
