// Digital circuit full_adder.dig as structural Verilog
module full_adder (
  input  C_in,
  input  B,
  input  A,
  output C_out,
  output S
);

  wire and_1_out, and_2_out, xor_1_out;

  xor xor_1 (xor_1_out, A, B);
  and and_1 (and_1_out, B, A);
  and and_2 (and_2_out, xor_1_out, C_in);
  xor xor_2 (S, xor_1_out, C_in);
  or or_1 (C_out, and_2_out, and_1_out);
endmodule
